// Digital circuit digitalodev1.dig as structural Verilog
module digitalodev1 (
  input  in_1,
  input  in_2,
  output out_3,
  output out_4
);

  wire and_1_out, or_1_out, xnor_1_out, xor_1_out;

  and and_1 (and_1_out, in_2, in_1);
  or or_1 (or_1_out, in_2, in_1);
  xor xor_1 (xor_1_out, in_2, in_1);
  xnor xnor_1 (xnor_1_out, in_2, in_1);
  nand nand_1 (out_3, and_1_out, or_1_out);
  LookUpTable lookuptable_1 (.in0(xor_1_out), .in1(xnor_1_out), .out(out_4));
endmodule
